# Fritzing sketch RaspberryPi-FlatDock (saved by Fritzing 0.8.0b)
breadboards: 1

parts:
  GPIO = double row female pin header, 26 pins [form="♀ (female)"]
  I2C_(1) = female pin header, 5 pins [form="♀ (female)"]
  Serial = female pin header, 5 pins [form="♀ (female)"]
  Digital-2 = female pin header, 5 pins [form="♀ (female)"]
  Digital-3 = female pin header, 5 pins [form="♀ (female)"]
  Power = LED - 5mm [color="White (4500K)" package="5 mm [THT]"]
  R1 = Resistor [tolerance=±5% resistance=220 package="0805 [SMD]"]
  SPI = female pin header, 5 pins [form="♀ (female)"]
  5_+ = mystery part, 2 pins [chip_label=? spacing=300mil]
  U1 = mystery part, 3 pins [chip_label=?]
  PF1 = Resistor [tolerance=±5% resistance=220 package="1206 [SMD]"]
  3_3VREG = Pad [width=3.907700991453 height=3.12615384615383 connect=center]  # not connected
  I2C_(2) = female pin header, 5 pins [form="♀ (female)"]
  3_3v = female pin header, 2 pins [form="♀ (female)"]
  J1 = female pin header, 2 pins [form="♀ (female)"]
  Digital-1 = female pin header, 5 pins [form="♀ (female)"]
  J2 = female pin header, 2 pins [form="♀ (female)"]
  I2C_(2)1 = female pin header, 5 pins [form="♀ (female)"]

nets:
  N1: GPIO.pin1, J1.pin1
  N2: GPIO.pin2, J1.pin2
  N3: GPIO.pin3, Digital-1.pin1
  N4: GPIO.pin5, Digital-1.pin2
  N5: GPIO.pin6, Digital-3.pin5
  N6: GPIO.pin8, Digital-3.pin3
  N7: GPIO.pin9, Serial.pin1
  N8: GPIO.pin10, Serial.pin2
  N9: GPIO.pin13, R1.Pin_1, 5_+.pin1, U1.pin1
  N10: GPIO.pin15, I2C_(1).pin4, I2C_(2).pin2, I2C_(2)1.pin2
  N11: GPIO.pin16, I2C_(1).pin5, I2C_(2).pin1, I2C_(2)1.pin1
  N12: GPIO.pin17, Digital-3.pin4
  N13: GPIO.pin19, Digital-2.pin3
  N14: GPIO.pin20, Digital-2.pin4
  N15: GPIO.pin21, Digital-2.pin5
  N16: GPIO.pin23, SPI.pin3
  N17: GPIO.pin24, SPI.pin2
  N18: GPIO.pin25, SPI.pin1
  N19: GPIO.pin26, Serial.pin5, SPI.pin5, 3_3v.pin1, J2.pin2
  N20: I2C_(1).pin1, Digital-1.pin5
  N21: I2C_(1).pin2, SPI.pin4, Digital-1.pin4, J2.pin1
  N22: Serial.pin4, PF1.Pin_0, 3_3v.pin2
  N23: Digital-2.pin1, I2C_(2).pin5
  N24: Digital-2.pin2, I2C_(2).pin4
  N25: Digital-3.pin1, I2C_(2)1.pin5
  N26: Digital-3.pin2, I2C_(2)1.pin4
  GND: Power.cathode, 5_+.pin2, U1.pin3
  N27: Power.anode, R1.Pin_0
  N28: U1.pin2, PF1.Pin_1

notes:
  -
  +
  Clixx.io
  i
  o
  c
  d
  *
  MOSI
  MISO
  SCLK
  i=7(4)
  o=4(23)
  *=1(18)
  i=2(21)
  o=3(22)
  *=0(17)
  i=5(24)
  o=6(25)
  CE0
  CE1
