# Fritzing sketch Demileuve (saved by Fritzing 0.8.0b)
breadboards: 1

parts:
  Digital-3_(3_3v) = female pin header, 5 pins [form="♀ (female)"]
  I2C = female pin header, 5 pins [form="♀ (female)"]
  Analog-1 = female pin header, 5 pins [form="♀ (female)"]
  Digital-2 = female pin header, 5 pins [form="♀ (female)"]
  Analog-2 = female pin header, 5 pins [form="♀ (female)"]
  LED1 = LED - 5mm [color="Red (633nm)" package="5 mm [THT]"]
  R3 = Resistor [tolerance=±5% resistance=1k package="0805 [SMD]"]
  R2 = Resistor [tolerance=±5% resistance=2.2k package="0805 [SMD]"]
  R1 = Resistor [tolerance=±5% resistance=4.7k package="0805 [SMD]"]
  C1 = Ceramic Capacitor [capacitance=1µF package="0805 [SMD, multilayer]"]
  Duemilanove = Netduino
  R5 = Resistor [tolerance=±5% resistance=220 package="0805 [SMD]"]
  R6 = Resistor [tolerance=±5% resistance=220 package="0805 [SMD]"]
  R7 = Resistor [tolerance=±5% resistance=220 package="0805 [SMD]"]
  5V = female pin header, 2 pins [form="♀ (female)"]
  5V_2 = female pin header, 2 pins [form="♀ (female)"]
  Digital-1 = female pin header, 5 pins [form="♀ (female)"]
  5V_3 = female pin header, 2 pins [form="♀ (female)"]

nets:
  N1: Digital-3_(3_3v).pin1, R5.Pin_1, R6.Pin_0
  N2: Digital-3_(3_3v).pin2, Duemilanove.D10_PWM3
  N3: Digital-3_(3_3v).pin4, Duemilanove.3V3, R7.Pin_1
  N4: Digital-3_(3_3v).pin5, I2C.pin1, Analog-1.pin1, Digital-2.pin5, Analog-2.pin1, LED1.cathode, Duemilanove.GND#1, Duemilanove.GND#20, R6.Pin_1, 5V.pin1, 5V_2.pin1, Digital-1.pin5, 5V_3.pin1
  N5: I2C.pin2, Analog-1.pin2, Digital-2.pin4, Analog-2.pin2, R3.Pin_1, R2.Pin_1, Duemilanove.+5V, 5V.pin2, 5V_2.pin2, Digital-1.pin4, 5V_3.pin2
  N6: I2C.pin3, Duemilanove.D2_RX1
  N7: I2C.pin4, R3.Pin_0, Duemilanove.A4_TWD
  N8: I2C.pin5, R2.Pin_0, Duemilanove.A5_TWCK
  N9: Analog-1.pin3, Duemilanove.D6_PWM1
  N10: Analog-1.pin4, Duemilanove.A0
  N11: Analog-1.pin5, R1.Pin_1, C1.0, C1.1
  N12: Digital-2.pin1, Duemilanove.D13_SPCK
  N13: Digital-2.pin2, Duemilanove.D12_MISO
  N14: Digital-2.pin3, Duemilanove.D11_MOSI
  N15: Analog-2.pin4, Duemilanove.A1
  N16: Analog-2.pin5, Duemilanove.D9_PWM2
  N17: LED1.anode, R7.Pin_0
  N18: R1.Pin_0, Duemilanove.D5_PWM0
  N19: Duemilanove.D8_CTS1, R5.Pin_0
  N20: Duemilanove.D7_RTS1, Digital-1.pin3
  N21: Duemilanove.D4_CS0, Digital-1.pin2
  N22: Duemilanove.D3_TX1, Digital-1.pin1

notes:
  +
  -
  *
  i
  o
  d
  c
  Analog 1
  Analog 2
  o - D5 (PWM + DAC)
  i - A0 (ADC)
  o - D9 (PWM)
  i - A1 (ADC)
  Digital 1
  Digital 2
  Digital 3
  i - D4
  o - D3
  i - D12
  o - D13
  i - D10
  o - D8 (3.3v)
  I2C
  SDA - A4
  * - D2
  SCL - A5
  clixx.io
  * - D11
  * - D6 (PWM)

// code stored in the sketch: toneMelody.ino
/*
  Melody
 
 Plays a melody 
 
 circuit:
 * 8-ohm speaker on digital pin 8
 
 created 21 Jan 2010
 modified 30 Aug 2011
 by Tom Igoe 

This example code is in the public domain.
 
 http://arduino.cc/en/Tutorial/Tone
 
 */
 #include "pitches.h"

// notes in the melody:
int melody[] = {
  NOTE_C4, NOTE_G3,NOTE_G3, NOTE_A3, NOTE_G3,0, NOTE_B3, NOTE_C4};

// note durations: 4 = quarter note, 8 = eighth note, etc.:
int noteDurations[] = {
  4, 8, 8, 4,4,4,4,4 };

void setup() {
  // iterate over the notes of the melody:
}

void loop() {
  // no need to repeat the melody.
  for (int thisNote = 0; thisNote < 8; thisNote++) {

    // to calculate the note duration, take one second 
    // divided by the note type.
    //e.g. quarter note = 1000 / 4, eighth note = 1000/8, etc.
    int noteDuration = 1000/noteDurations[thisNote];
    tone(2, melody[thisNote],noteDuration);

    // to distinguish the notes, set a minimum time between them.
    // the note's duration + 30% seems to work well:
    int pauseBetweenNotes = noteDuration * 1.30;
    delay(pauseBetweenNotes);
    // stop the tone playing:
    noTone(2);
  }
}
