# Fritzing sketch PIC8pinSOIC (saved by Fritzing 0.8.0b)
breadboards: 1

parts:
  i_o = female pin header, 2 pins [form="♀ (female)"]
  +_- = female pin header, 2 pins [form="♀ (female)"]
  clixx_io = Tantalum Capacitor [capacitance="1 μF" package="A 3216 [SMD, tantalum]"]
  PIC16F = SO08 [chip_label=IC package=SO]
  Digital-1 = female pin header, 5 pins [form="♀ (female)"]
  Digital-2 = female pin header, 5 pins [form="♀ (female)"]
  -_+ = female pin header, 2 pins [form="♀ (female)"]
  + = Pad [width=1 height=3 connect=center]
  - = Pad [width=1 height=3 connect=center]
  o = Pad [width=1 height=3 connect=center]
  i = Pad [width=1 height=3 connect=center]
  Pad1 = Pad [width=0.7 height=1.5 connect=center]
  Pad4 = Pad [width=0.7 height=1.5 connect=center]
  Pad5 = Pad [width=0.7 height=1.5 connect=center]
  Pad6 = Pad [width=0.7 height=1.5 connect=center]
  Pad7 = Pad [width=0.7 height=1.5 connect=center]
  Pad8 = Pad [width=0.7 height=1.5 connect=center]
  Pad2 = Pad [width=0.7 height=1.5 connect=center]
  Pad3 = Pad [width=0.7 height=1.5 connect=center]
  Pad9 = Pad [width=1.7 height=4 connect=center]  # not connected
  Pad10 = Pad [width=1.7 height=4 connect=center]  # not connected

nets:
  N1: i_o.pin1, PIC16F.6, Digital-1.pin1, Pad6.pad
  N2: i_o.pin2, PIC16F.7, Digital-1.pin2, Pad7.pad
  N3: +_-.pin1, clixx_io.+, PIC16F.1, Digital-1.pin4, Digital-2.pin4, -_+.pin2, +.pad, Pad1.pad
  GND: +_-.pin2, clixx_io.-, PIC16F.8, Digital-1.pin5, Digital-2.pin5, -_+.pin1, -.pad, Pad8.pad
  N4: PIC16F.2, Digital-2.pin1, i.pad, Pad2.pad
  N5: PIC16F.3, Digital-2.pin2, o.pad, Pad3.pad
  N6: PIC16F.4, Digital-1.pin3, Pad4.pad
  N7: PIC16F.5, Digital-2.pin3, Pad5.pad

notes:
  *
  o
  i
  -
  +
  *=5
  i=3
  *=4
  o=6
  i=7
  o=2
  r0.1
