# Fritzing sketch Breakout-SOIC8 (saved by Fritzing 0.8.0b)
breadboards: 1

parts:
  o_i = female pin header, 2 pins [form="♀ (female)"]
  +_- = female pin header, 2 pins [form="♀ (female)"]
  o_i_2 = female pin header, 2 pins [form="♀ (female)"]
  +_-_2 = female pin header, 2 pins [form="♀ (female)"]
  IC1 = SO08 [chip_label=IC spacing=300mil package=SO]
  J1 = female pin header, 1 pin [form="♀ (female)"]
  J2 = female pin header, 2 pins [form="♀ (female)"]
  J3 = female pin header, 4 pins [form="♀ (female)"]
  J4 = female pin header, 4 pins [form="♀ (female)"]
  J5 = female pin header, 1 pin [form="♀ (female)"]
  J6 = female pin header, 1 pin [form="♀ (female)"]
  J7 = female pin header, 1 pin [form="♀ (female)"]
  o_i1 = female pin header, 2 pins [form="♀ (female)"]
  J8 = female pin header, 1 pin [form="♀ (female)"]  # not connected
  J9 = female pin header, 1 pin [form="♀ (female)"]  # not connected
  J10 = double row female pin header, 14 pins [form="♀ (female)"]  # not connected
  C1 = Tantalum Capacitor [capacitance="1 μF" package="A 3216 [SMD, tantalum]"]

nets:
  N1: o_i.pin1, J2.pin1
  N2: o_i.pin2, J2.pin2
  N3: +_-.pin1, J5.pin1, C1.+
  GND: +_-.pin2, J1.pin1, C1.-
  N4: o_i_2.pin1, o_i1.pin2
  N5: o_i_2.pin2, o_i1.pin1
  N6: +_-_2.pin1, J6.pin1
  N7: +_-_2.pin2, J7.pin1
  N8: IC1.1, J4.pin4
  N9: IC1.2, J4.pin3
  N10: IC1.3, J4.pin2
  N11: IC1.4, J4.pin1
  N12: IC1.5, J3.pin1
  N13: IC1.6, J3.pin2
  N14: IC1.7, J3.pin3
  N15: IC1.8, J3.pin4

notes:
  i
  o
  -
  +
  Out->
  <-In
