# Fritzing sketch digital-input-button_Button (saved by Fritzing 0.8.3b)
circuit board: 2.92478cm x 5.58617cm
breadboards: 1

parts:
  +_- = mystery part, 2 pins [chip_label=PWR-IN]
  o_i = mystery part, 2 pins [chip_label=DATA-IN]
  +_-_2 = mystery part, 2 pins [chip_label=PWR-OUT]
  i_o = mystery part, 2 pins [chip_label=DATA-OUT]
  R1 = Resistor [tolerance=±5% resistance=10k package="0805 [SMD]"]
  LED = smd LED [color="Blue (505nm)" package="0805 [SMD]"]
  R2 = Resistor [tolerance=±5% resistance=10k package="0805 [SMD]"]
  U1 = mystery part, 1 pin [chip_label=?]
  U2 = mystery part, 1 pin [chip_label=?]
  J1 = female pin header, 1 pin [form="♀ (female)"]
  J2 = female pin header, 1 pin [form="♀ (female)"]
  Pad1 = Pad [width=1.22296296296297 height=3.19851851851851 connect=center]  # not connected
  Pad2 = Pad [width=1.22296296296297 height=3.19851851851851 connect=center]  # not connected
  Pad3 = Pad [width=1.22296296296297 height=3.19851851851851 connect=center]  # not connected
  Pad4 = Pad [width=1.22296296296297 height=3.19851851851851 connect=center]  # not connected

nets:
  N1: +_-.pin1, +_-_2.pin2, i_o.pin2, R1.Pin_1, LED.cathode
  N2: +_-.pin2, +_-_2.pin1, U1.pin1, J1.pin1
  N3: o_i.pin1, i_o.pin1, R1.Pin_0, U2.pin1, J2.pin1
  N4: o_i.pin2, R2.Pin_1
  N5: LED.anode, R2.Pin_0

notes:
  In this example, a pushbutton is used as a digital input and an LED is a digital output. Related example: http://arduino.cc/en/Tutorial/Button
