# Fritzing sketch digital-temp-LM75A (saved by Fritzing 0.8.3b)
circuit board: 2.92478cm x 5.58617cm
breadboards: 1

parts:
  +_- = mystery part, 2 pins [chip_label=PWR-IN]
  d_c = mystery part, 2 pins [chip_label=DATA-IN]
  +_-_2 = mystery part, 2 pins [chip_label=PWR-OUT]
  d_c_2 = mystery part, 2 pins [chip_label=DATA-OUT]
  R2 = Resistor [tolerance=±5% resistance=10k package="0805 [SMD]"]
  PWR = smd LED [color="Red (633nm)" package="0805 [SMD]"]
  TEMP_SENSOR = SO08 [chip_label=IC package=SO]
  C1 = Tantalum Capacitor [capacitance="1 μF" package="A 3216 [SMD, tantalum]"]
  Pad14 = Pad [width=1.61270647619049 height=0.56444565396826 connect=center]
  Pad15 = Pad [width=1.61270647619049 height=0.56444565396826 connect=center]
  Pad16 = Pad [width=1.61270647619049 height=0.56444565396826 connect=center]
  Pad17 = Pad [width=1.61270647619049 height=0.56444565396826 connect=center]
  Pad18 = Pad [width=1.61270647619049 height=0.56444565396826 connect=center]
  Pad19 = Pad [width=1.61270647619049 height=0.56444565396826 connect=center]
  Pad20 = Pad [width=1.61270647619049 height=0.56444565396826 connect=center]  # not connected
  Pad21 = Pad [width=1.61270647619049 height=0.56444565396826 connect=center]
  Pad22 = Pad [width=1.61270647619049 height=0.56444565396826 connect=center]  # not connected

nets:
  N1: +_-.pin1, +_-_2.pin2, PWR.cathode, TEMP_SENSOR.4, TEMP_SENSOR.7, C1.-, Pad15.pad, Pad19.pad
  N2: +_-.pin2, +_-_2.pin1, R2.Pin_1, TEMP_SENSOR.8, C1.+, Pad21.pad
  N3: d_c.pin1, d_c_2.pin2, TEMP_SENSOR.1
  N4: d_c.pin2, d_c_2.pin1, TEMP_SENSOR.2
  N5: R2.Pin_0, PWR.anode
  N6: TEMP_SENSOR.5, Pad16.pad, Pad17.pad
  N7: TEMP_SENSOR.6, Pad14.pad, Pad18.pad

notes:
  In this example, a pushbutton is used as a digital input and an LED is a digital output. Related example: http://arduino.cc/en/Tutorial/Button
