# Fritzing sketch Display-I2C-8x2LCD-icback (saved by Fritzing 0.8.0b)
breadboards: 1

parts:
  J2 = female pin header, 5 pins [form="♀ (female)"]
  LCD1 = LCD screen
  R1 = Trimmer Potentiometer [maximum_resistance=10kΩ package=THT]
  MCP9808 = MCP9808-SSOP20 [part_number=MCP9808-E/SS chip_label=IC package=SSOP20]

nets:
  VSS: J2.pin1, LCD1.VSS, LCD1.R/W, LCD1.LED-, R1.leg2, MCP9808.VSS
  VDD: J2.pin2, LCD1.VDD, LCD1.LED+, R1.leg1, MCP9808.RESET, MCP9808.VCC
  N1: J2.pin3, MCP9808.INT
  N2: J2.pin4, MCP9808.SDA
  N3: J2.pin5, MCP9808.SCL
  N4: LCD1.V0, R1.wiper
  N5: LCD1.RS, MCP9808.GP5
  N6: LCD1.E, MCP9808.GP4
  N7: LCD1.DB4, MCP9808.GP0
  N8: LCD1.DB5, MCP9808.GP1
  N9: LCD1.DB6, MCP9808.GP2
  N10: LCD1.DB7, MCP9808.GP3

notes:
  Clixx.io
  - + i d c
