# Fritzing sketch Display-Nokia5110 (saved by Fritzing 0.7.12b)
breadboards: 1

parts:
  J2 = female pin header, 5 pins [form="♀ (female)"]
  CE_DC = female pin header, 2 pins [form="♀ (female)"]
  J3 = female pin header, 8 pins [form="♀ (female)"]

nets:
  N1: J2.pin1, J3.pin1
  N2: J2.pin2, J3.pin2, J3.pin3
  N3: J2.pin3, J3.pin4
  N4: J2.pin4, J3.pin8
  N5: J2.pin5, J3.pin5
  N6: CE_DC.pin1, J3.pin6
  N7: CE_DC.pin2, J3.pin7

notes:
  Clixx.io
  - + c r i
