# Fritzing sketch Power-ButtonBattery (saved by Fritzing 0.7.12b)
breadboards: 1

parts:
  i_o = female pin header, 2 pins [form="♀ (female)"]
  + = Pad [width=1 height=3 connect=center]  # not connected
  - = Pad [width=1 height=3 connect=center]  # not connected
  i = Pad [width=1 height=3 connect=center]  # not connected
  +_- = female pin header, 2 pins [form="♀ (female)"]
  +_-_2 = female pin header, 2 pins [form="♀ (female)"]
  i_o_2 = female pin header, 2 pins [form="♀ (female)"]
  o = Pad [width=1 height=3 connect=center]  # not connected
  R1 = Resistor [tolerance=±5% resistance=220 package="0805 [SMD]"]
  VCC1 = Battery

nets:
  N1: i_o.pin1, R1.Pin_0
  N2: i_o.pin2, i_o_2.pin2
  N3: +_-.pin1, +_-_2.pin1, R1.Pin_1, VCC1.+
  GND: +_-.pin2, +_-_2.pin2, i_o_2.pin1, VCC1.-

notes:
  r0.1
  Voltmeter
