# Fritzing sketch power-variable-lm317 (saved by Fritzing 0.8.3b)
circuit board: 2.92478cm x 5.58617cm
breadboards: 1

parts:
  i_o = female pin header, 2 pins [form="♀ (female)"]
  VREG = SO08 [chip_label=IC package=SO]
  + = Pad [width=1 height=3 connect=center]  # not connected
  - = Pad [width=1 height=3 connect=center]  # not connected
  i = Pad [width=1 height=3 connect=center]  # not connected
  +_- = female pin header, 2 pins [form="♀ (female)"]
  +_-1 = female pin header, 2 pins [form="♀ (female)"]
  i_o1 = female pin header, 2 pins [form="♀ (female)"]
  R1 = Resistor [tolerance=±5% resistance=220 package="0805 [SMD]"]
  R2 = Trimmer Potentiometer [maximum_resistance=10kΩ package=THT]
  o = Pad [width=1 height=3 connect=center]  # not connected

nets:
  N1: i_o.pin1, i_o1.pin1
  N2: i_o.pin2, i_o1.pin2
  N3: VREG.1, +_-1.pin1
  N4: VREG.2, VREG.3, VREG.6, VREG.7, +_-.pin1, R1.Pin_0
  N5: VREG.4, R1.Pin_1, R2.leg2
  GND: +_-.pin2, +_-1.pin2, R2.leg1

notes:
  i=PB2
  o=PB1
  *=PB5
  r0.2
