# Fritzing sketch power-mosfet-n (saved by Fritzing 0.8.0b)
breadboards: 1

parts:
  i_o = female pin header, 2 pins [form="♀ (female)"]
  +_- = female pin header, 2 pins [form="♀ (female)"]
  R1 = Resistor [tolerance=±5% resistance=220 package="0805 [SMD]"]
  Q1 = Basic FET N-Channel [package="DPak [SMD]"]
  D1 = Rectifier Diode [part_number=1N4001 package="Melf DO-213 AB [SMD]"]
  D2 = Rectifier Diode [part_number=1N4001 package="Melf DO-213 AB [SMD]"]
  +_-_-_+ = screw terminal, 4 pins
  Pad1 = Pad [width=0.948266666666666 height=2.16746666666666 connect=center]  # not connected
  C1 = Electrolytic Capacitor [capacitance=1µF package="100 mil [THT, electrolytic]"]  # not connected
  Pad2 = Pad [width=0.948266666666666 height=2.16746666666666 connect=center]  # not connected
  Pad3 = Pad [width=0.948266666666666 height=2.16746666666666 connect=center]  # not connected
  R2 = Resistor [tolerance=±5% resistance=220 package="0805 [SMD]"]

nets:
  N1: i_o.pin2, R2.Pin_0
  GND: +_-.pin2, R1.Pin_0, Q1.source
  N2: R1.Pin_1, Q1.Gate, R2.Pin_1
  N3: Q1.drain, D1.cathode
  N4: D1.anode, +_-_-_+.pin2
  N5: D2.anode, +_-_-_+.pin3
  N6: +_-_-_+.pin1, +_-_-_+.pin4

notes:
  Input <<
  r0.2
  Motor >>
  Power <<
