# Fritzing sketch power-voltmeter (saved by Fritzing 0.8.0b)
breadboards: 1

parts:
  i_o = female pin header, 2 pins [form="♀ (female)"]
  + = Pad [width=1 height=3 connect=center]  # not connected
  - = Pad [width=1 height=3 connect=center]  # not connected
  i = Pad [width=1 height=3 connect=center]  # not connected
  +_- = female pin header, 2 pins [form="♀ (female)"]
  +_-_2 = female pin header, 2 pins [form="♀ (female)"]
  i_o_2 = female pin header, 2 pins [form="♀ (female)"]
  o = Pad [width=1 height=3 connect=center]  # not connected
  J1 = female pin header, 3 pins [form="♀ (female)"]

nets:
  N1: i_o.pin1, i_o_2.pin1
  N2: i_o.pin2, i_o_2.pin2
  N3: +_-.pin1, +_-_2.pin1, J1.pin2, J1.pin3
  GND: +_-.pin2, +_-_2.pin2, J1.pin1

notes:
  +  +  -
  r0.2
  << Output
