# Fritzing sketch Attiny-ISP-Adaptor (saved by Fritzing 0.8.3b)
circuit board: 2.92478cm x 5.58617cm
breadboards: 1

parts:
  i_o = female pin header, 2 pins [form="♀ (female)"]  # not connected
  Digital-1 = female pin header, 5 pins [form="♀ (female)"]
  Digital-2 = female pin header, 5 pins [form="♀ (female)"]
  -_+ = female pin header, 2 pins [form="♀ (female)"]
  +_- = female pin header, 2 pins [form="♀ (female)"]
  ISP = shrouded pin header, 6 pins [form="♂ (shrouded male)"]

nets:
  N1: Digital-1.pin1, ISP.pin1
  N2: Digital-1.pin2, ISP.pin2
  N3: Digital-1.pin3, ISP.pin3
  N4: Digital-1.pin4, Digital-2.pin4, -_+.pin2, +_-.pin1, ISP.pin6
  N5: Digital-1.pin5, Digital-2.pin5, -_+.pin1, ISP.pin4
  N6: Digital-2.pin3, ISP.pin5
  GND: +_-.pin2

notes:
  -
  r0.2
