# Fritzing sketch radio-i2c-tea5767 (saved by Fritzing 0.8.0b)
breadboards: 1

parts:
  d_c = female pin header, 2 pins [form="♀ (female)"]
  + = Pad [width=1 height=3 connect=center]  # not connected
  - = Pad [width=1 height=3 connect=center]  # not connected
  i = Pad [width=1 height=3 connect=center]  # not connected
  +_- = female pin header, 2 pins [form="♀ (female)"]
  +_-_2 = female pin header, 2 pins [form="♀ (female)"]
  L_R = female pin header, 2 pins [form="♀ (female)"]
  o = Pad [width=1 height=3 connect=center]  # not connected
  Antenae = female pin header, 1 pin [form="♀ (female)"]
  1-4 = female pin header, 5 pins [form="♀ (female)"]
  5-8 = female pin header, 5 pins [form="♀ (female)"]

nets:
  N1: d_c.pin1, 1-4.pin1
  N2: d_c.pin2, 1-4.pin2
  N3: +_-.pin1, +_-_2.pin1, 1-4.pin4
  GND: +_-.pin2, +_-_2.pin2, 1-4.pin3, 5-8.pin5
  N4: L_R.pin1, 5-8.pin3
  N5: L_R.pin2, 5-8.pin4
  N6: Antenae.pin1, 5-8.pin1

notes:
  << Input
  r0.2
  << Output
